# Fritzing sketch Car_Sparkfun01 (saved by Fritzing 0.9.2b)
breadboards: 1

parts:
  M1 = DC Motor  # not connected
  M2 = DC Motor  # not connected
  VCC1 = 4 x AAA Battery Mount
  D1 = Schottky Diode [part_number=1N5817 package="300 mil [THT]"]
  U1 = EDISON  # not connected

nets:
  N1: VCC1.+, D1.cathode

notes:
  1.2x4 = 4.8V
  6V
